# Fritzing sketch button (saved by Fritzing 0.9.2b)
stripboards: 1

parts:
  part = Raspberry Pi 2
  LED1 = LED - 5mm [color="Red (660nm)" package="5 mm [THT]"]
  TIP120 = NPN-Transistor [package="TO92 [THT]"]
  R1 = Resistor [tolerance=±5% resistance=10k package=THT]
  pushbutton = Round Pushbutton

nets:
  3V3: part.3v3, part.3V3, pushbutton.leg1
  N1: part.GPIO25, TIP120.B
  N2: part.GPIO24, R1.Pin_1, pushbutton.leg0
  12V: LED1.cathode
  N3: LED1.anode, TIP120.C
  GND: TIP120.E, R1.Pin_0
