# Fritzing sketch basic schematic (saved by Fritzing 0.9.2b)
breadboards: 1

parts:
  TIP120 = NPN-Transistor [package="TO92 [THT]"]
  Pump = DC Motor
  part = Raspberry Pi 2
  D1 = Rectifier Diode [part_number=1N4001 package="300 mil [THT]"]

nets:
  GND: TIP120.E
  N1: TIP120.B, part.GPIO24
  N2: TIP120.C, Pump.pin_2, D1.anode
  12V: Pump.pin_1, D1.cathode
